// Logisim project assignment.circ as structural Verilog: 15 circuits, main circuit main
module main (
  input  RESET,
  input  [7:0] in_2,
  input  [2:0] M,
  output [7:0] out_4,
  output [3:0] out_5
);

  wire and_1_out, clock_1_out, clock_2_out, cnt_1_last, decoder_1_out0, multiplexer_1_out, not_1_out,
       not_2_out, t_ff_1_q, t_ff_1_qn;
  wire [3:0] ad_4bit_1_s, cnt_1_c, find_a_1_out_1;
  wire [7:0] find_q_1_out_1;

  AD_4BIT ad_4bit_1 (.A(out_5), .B(M), .SUB(1'b1), .S(ad_4bit_1_s));  // open: COUT
  and and_1 (and_1_out, not_1_out, decoder_1_out0);
  not not_1 (not_1_out, cnt_1_last);
  Decoder #(.enable("false"), .select(4)) decoder_1 (
    .out0(decoder_1_out0), .sel(cnt_1_c));  // open: out1, out2, out3, out4, out5, out6, out7, out8, out9, out10, out11, out12, out13, out14, out15
  not not_2 (not_2_out, ad_4bit_1_s[3]);
  T_Flip_Flop t_ff_1 (.T(1'b1), .clk(clock_1_out), .Q(t_ff_1_q), .Qn(t_ff_1_qn), .reset(RESET));  // open: preset
  Clock clock_1 (.out(clock_1_out));
  FIND_Q find_q_1 (.IN_1(in_2), .Q(out_4), .LOAD(and_1_out), .OUT_1(find_q_1_out_1));
  FIND_A find_a_1 (
    .KEEP(ad_4bit_1_s[3]), .IN_1(4'b0000), .S(ad_4bit_1_s), .LOAD(and_1_out), .A(out_5),
    .OUT_1(find_a_1_out_1));
  Multiplexer multiplexer_1 (.in0(not_2_out), .in1(find_q_1_out_1[0]), .out(multiplexer_1_out), .sel(and_1_out));
  CNT cnt_1 (.CLK(t_ff_1_q), .RESET(RESET), .LAST(cnt_1_last), .C(cnt_1_c));
  // Probe on cnt_1_last
  // Probe on cnt_1_c
  Clock clock_2 (.out(clock_2_out));
  // Shift_Register #(.length(12)) shift_register_1: pin names not known; wires that end beside it: RESET, clock_2_out, 1'b0, multiplexer_1_out, find_q_1_out_1[1], find_q_1_out_1[2], find_q_1_out_1[3], find_q_1_out_1[4], find_q_1_out_1[5], find_q_1_out_1[6], find_q_1_out_1[7], t_ff_1_qn
endmodule

module DFF_from_JK (
  input  D,
  input  CLK,
  input  RESET,
  output Q
);

  wire not_1_out;

  not not_1 (not_1_out, D);
  J_K_Flip_Flop j_k_ff_1 (.J(D), .K(not_1_out), .clk(CLK), .Q(Q), .reset(RESET));  // open: Qn, preset
endmodule

module AD_1BIT (
  input  A,
  input  B,
  input  CIN,
  output S,
  output COUT
);

  wire and_1_out, and_2_out, xor_1_out;

  xor xor_1 (xor_1_out, A, B);
  and and_1 (and_1_out, A, B);
  xor xor_2 (S, xor_1_out, CIN);
  and and_2 (and_2_out, CIN, xor_1_out);
  or or_1 (COUT, and_1_out, and_2_out);
endmodule

module AD_4BIT (
  input  [3:0] A,
  input  [2:0] B,
  input  SUB,
  output [3:0] S,
  output COUT
);

  wire ad_1bit_1_cout, ad_1bit_2_cout, ad_1bit_3_cout, xor_1_out, xor_2_out, xor_3_out, xor_4_out;

  xor xor_1 (xor_1_out, B[0], SUB);
  xor xor_2 (xor_2_out, B[1], SUB);
  xor xor_3 (xor_3_out, B[2], SUB);
  xor xor_4 (xor_4_out, 1'b0, SUB);
  AD_1BIT ad_1bit_1 (.A(A[0]), .B(xor_1_out), .CIN(SUB), .S(S[0]), .COUT(ad_1bit_1_cout));
  AD_1BIT ad_1bit_2 (.A(A[1]), .B(xor_2_out), .CIN(ad_1bit_1_cout), .S(S[1]), .COUT(ad_1bit_2_cout));
  AD_1BIT ad_1bit_3 (.A(A[2]), .B(xor_3_out), .CIN(ad_1bit_2_cout), .S(S[2]), .COUT(ad_1bit_3_cout));
  AD_1BIT ad_1bit_4 (.A(A[3]), .B(xor_4_out), .CIN(ad_1bit_3_cout), .S(S[3]), .COUT(COUT));
endmodule

module shift (
  input  Q0_VAL,
  input  SETQ0_OVER,
  input  LOAD,
  input  SHIFT,
  input  [7:0] N,
  input  CLK,
  input  [3:0] RIM,
  input  RLOAD,
  output [7:0] Q1,
  output [3:0] R
);

  wire multiplexer_1_out, multiplexer_2_out, multiplexer_3_out, multiplexer_4_out, multiplexer_5_out,
       multiplexer_6_out, multiplexer_7_out, multiplexer_8_out, multiplexer_9_out, multiplexer_10_out,
       multiplexer_11_out, multiplexer_12_out, multiplexer_13_out, multiplexer_14_out, not_1_out;
  wire [0:0] and_1_out;

  not not_1 (not_1_out, LOAD);
  and and_1 (and_1_out[0], not_1_out, SHIFT);
  Multiplexer #(.select(2)) multiplexer_1 (
    .in0(Q1[1]), .in1(Q1[0]), .in2(N[1]), .in3(1'b0), .out(multiplexer_1_out), .sel({LOAD, and_1_out[0]}));
  Multiplexer #(.select(2)) multiplexer_2 (
    .in0(Q1[2]), .in1(Q1[1]), .in2(N[2]), .in3(1'b0), .out(multiplexer_2_out), .sel({LOAD, and_1_out[0]}));
  Multiplexer #(.select(2)) multiplexer_3 (
    .in0(Q1[4]), .in1(Q1[3]), .in2(N[4]), .in3(1'b0), .out(multiplexer_3_out), .sel({LOAD, and_1_out[0]}));
  Multiplexer #(.select(2)) multiplexer_4 (
    .in0(Q1[6]), .in1(Q1[5]), .in2(N[6]), .in3(1'b0), .out(multiplexer_4_out), .sel({LOAD, and_1_out[0]}));
  Multiplexer #(.select(2)) multiplexer_5 (
    .in0(R[1]), .in1(R[0]), .in2(RIM[1]), .in3(1'b0), .out(multiplexer_5_out), .sel({RLOAD, and_1_out[0]}));
  Multiplexer #(.select(2)) multiplexer_6 (
    .in0(R[2]), .in1(R[1]), .in2(RIM[2]), .in3(1'b0), .out(multiplexer_6_out), .sel({RLOAD, and_1_out[0]}));
  Multiplexer #(.select(2)) multiplexer_7 (
    .in0(Q1[0]), .in1(1'b0), .in2(N[0]), .in3(1'b0), .out(multiplexer_7_out), .sel({LOAD, and_1_out[0]}));
  Multiplexer #(.select(2)) multiplexer_8 (
    .in0(Q1[3]), .in1(Q1[2]), .in2(N[3]), .in3(1'b0), .out(multiplexer_8_out), .sel({LOAD, and_1_out[0]}));
  Multiplexer #(.select(2)) multiplexer_9 (
    .in0(Q1[5]), .in1(Q1[4]), .in2(N[5]), .in3(1'b0), .out(multiplexer_9_out), .sel({LOAD, and_1_out[0]}));
  Multiplexer #(.select(2)) multiplexer_10 (
    .in0(Q1[7]), .in1(Q1[6]), .in2(N[7]), .in3(1'b0), .out(multiplexer_10_out), .sel({LOAD, and_1_out[0]}));
  Multiplexer multiplexer_11 (.in0(multiplexer_13_out), .in1(RIM[0]), .out(multiplexer_11_out), .sel(RLOAD));
  Multiplexer #(.select(2)) multiplexer_12 (
    .in0(R[3]), .in1(R[2]), .in2(RIM[3]), .in3(1'b0), .out(multiplexer_12_out), .sel({RLOAD, and_1_out[0]}));
  Multiplexer #(.select(2)) multiplexer_13 (
    .in0(R[0]), .in1(Q1[7]), .in2(RIM[0]), .in3(1'b0), .out(multiplexer_13_out), .sel({LOAD, and_1_out[0]}));
  Multiplexer multiplexer_14 (.in0(multiplexer_7_out), .in1(Q0_VAL), .out(multiplexer_14_out), .sel(SETQ0_OVER));
  DFF_from_JK dff_from_jk_1 (.D(multiplexer_14_out), .CLK(CLK), .Q(Q1[0]));  // open: RESET
  DFF_from_JK dff_from_jk_2 (.D(multiplexer_1_out), .CLK(CLK), .Q(Q1[1]));  // open: RESET
  DFF_from_JK dff_from_jk_3 (.D(multiplexer_2_out), .CLK(CLK), .Q(Q1[2]));  // open: RESET
  DFF_from_JK dff_from_jk_4 (.D(multiplexer_8_out), .CLK(CLK), .Q(Q1[3]));  // open: RESET
  DFF_from_JK dff_from_jk_5 (.D(multiplexer_3_out), .CLK(CLK), .Q(Q1[4]));  // open: RESET
  DFF_from_JK dff_from_jk_6 (.D(multiplexer_9_out), .CLK(CLK), .Q(Q1[5]));  // open: RESET
  DFF_from_JK dff_from_jk_7 (.D(multiplexer_4_out), .CLK(CLK), .Q(Q1[6]));  // open: RESET
  DFF_from_JK dff_from_jk_8 (.D(multiplexer_10_out), .CLK(CLK), .Q(Q1[7]));  // open: RESET
  DFF_from_JK dff_from_jk_9 (.D(multiplexer_11_out), .CLK(CLK), .Q(R[0]));  // open: RESET
  DFF_from_JK dff_from_jk_10 (.D(multiplexer_5_out), .CLK(CLK), .Q(R[1]));  // open: RESET
  DFF_from_JK dff_from_jk_11 (.D(multiplexer_6_out), .CLK(CLK), .Q(R[2]));  // open: RESET
  DFF_from_JK dff_from_jk_12 (.D(multiplexer_12_out), .CLK(CLK), .Q(R[3]));  // open: RESET
endmodule

module DIVISOR_3BIT (
  input  [2:0] D_in,
  input  LOADD,
  input  CL
);

  wire dff_from_jk_1_q, dff_from_jk_2_q, dff_from_jk_3_q, multiplexer_1_out, multiplexer_2_out,
       multiplexer_3_out;

  Multiplexer multiplexer_1 (.in0(dff_from_jk_1_q), .in1(D_in[0]), .out(multiplexer_1_out), .sel(LOADD));
  Multiplexer multiplexer_2 (.in0(dff_from_jk_3_q), .in1(D_in[2]), .out(multiplexer_2_out), .sel(LOADD));
  Multiplexer multiplexer_3 (.in0(dff_from_jk_2_q), .in1(D_in[1]), .out(multiplexer_3_out), .sel(LOADD));
  DFF_from_JK dff_from_jk_1 (.D(multiplexer_1_out), .CLK(CL), .Q(dff_from_jk_1_q));  // open: RESET
  DFF_from_JK dff_from_jk_2 (.D(multiplexer_3_out), .CLK(CL), .Q(dff_from_jk_2_q));  // open: RESET
  DFF_from_JK dff_from_jk_3 (.D(multiplexer_2_out), .CLK(CL), .Q(dff_from_jk_3_q));  // open: RESET
endmodule

module ADD_4BIT (
  input  [2:0] D_in,
  input  LOADD,
  input  CL
);

  wire multiplexer_1_out, multiplexer_2_out, multiplexer_3_out;
  wire [2:0] dff_from_jk_1_q;

  Multiplexer multiplexer_1 (.in0(dff_from_jk_1_q[0]), .in1(D_in[0]), .out(multiplexer_1_out), .sel(LOADD));
  Multiplexer multiplexer_2 (.in0(dff_from_jk_1_q[1]), .in1(D_in[1]), .out(multiplexer_2_out), .sel(LOADD));
  Multiplexer multiplexer_3 (.in0(dff_from_jk_1_q[2]), .in1(D_in[2]), .out(multiplexer_3_out), .sel(LOADD));
  DFF_from_JK dff_from_jk_1 (.D(multiplexer_1_out), .CLK(CL), .Q(dff_from_jk_1_q[0]));  // open: RESET
  DFF_from_JK dff_from_jk_2 (.D(multiplexer_2_out), .CLK(CL), .Q(dff_from_jk_1_q[1]));  // open: RESET
  DFF_from_JK dff_from_jk_3 (.D(multiplexer_3_out), .CLK(CL), .Q(dff_from_jk_1_q[2]));  // open: RESET
endmodule

module CNT (
  input  CLK,
  input  RESET,
  output LAST,
  output [3:0] C
);

  wire and_1_out, and_2_out, decoder_1_out1, not_1_out, xor_1_out, xor_2_out, xor_3_out;

  DFF_from_JK dff_from_jk_1 (.D(not_1_out), .CLK(CLK), .RESET(RESET), .Q(C[0]));
  DFF_from_JK dff_from_jk_2 (.D(xor_1_out), .CLK(CLK), .RESET(RESET), .Q(C[1]));
  DFF_from_JK dff_from_jk_3 (.D(xor_2_out), .CLK(CLK), .RESET(RESET), .Q(C[2]));
  DFF_from_JK dff_from_jk_4 (.D(xor_3_out), .CLK(CLK), .RESET(RESET), .Q(C[3]));
  Decoder #(.enable("false"), .select(3)) decoder_1 (
    .out1(decoder_1_out1), .sel(C[2:0]));  // open: out0, out2, out3, out4, out5, out6, out7
  xor xor_1 (xor_1_out, C[0], C[1]);
  and and_1 (and_1_out, C[1], C[0]);
  not not_1 (not_1_out, C[0]);
  and and_2 (and_2_out, C[2], and_1_out);
  xor xor_2 (xor_2_out, and_1_out, C[2]);
  xor xor_3 (xor_3_out, C[3], and_2_out);
  and and_3 (LAST, decoder_1_out1, C[3]);
endmodule

module CTRL_FSM (
  input  START,
  input  CLC,
  input  RESET,
  input  LASTT,
  input  NEG,
  output LOAD_DIV,
  output CNT_CLR2,
  output SHIFT2,
  output LOAD_Q,
  output RLOAD2,
  output CNT_EN2,
  output SUB_MOD2,
  output SETQ0_OVER2,
  output Q0_VAL2,
  output DONE
);

  wire and_1_out, and_2_out, and_3_out, and_4_out, and_5_out, and_6_out, decoder_1_out0, decoder_1_out4,
       not_1_out, not_2_out, not_3_out, or_1_out, or_2_out, or_3_out, or_4_out, or_5_out, or_6_out, or_7_out,
       or_8_out, or_9_out, or_10_out, or_11_out, or_12_out;
  wire [2:0] dff_from_jk_3_q;

  DFF_from_JK dff_from_jk_1 (.D(or_12_out), .CLK(CLC), .RESET(RESET), .Q(dff_from_jk_3_q[2]));
  DFF_from_JK dff_from_jk_2 (.D(or_9_out), .CLK(CLC), .RESET(RESET), .Q(dff_from_jk_3_q[1]));
  DFF_from_JK dff_from_jk_3 (.D(or_6_out), .CLK(CLC), .RESET(RESET), .Q(dff_from_jk_3_q[0]));
  Decoder #(.select(3)) decoder_1 (
    .out0(decoder_1_out0), .out1(CNT_CLR2), .out2(SHIFT2), .out3(SUB_MOD2), .out4(decoder_1_out4),
    .out5(SETQ0_OVER2), .out6(CNT_EN2), .out7(DONE), .sel(dff_from_jk_3_q), .en(1'b1));
  not not_1 (not_1_out, START);
  and and_1 (and_1_out, START, decoder_1_out0);
  not not_2 (not_2_out, NEG);
  and and_2 (and_2_out, not_1_out, decoder_1_out0);
  and and_3 (and_3_out, SUB_MOD2, NEG);
  and and_4 (and_4_out, CNT_EN2, LASTT);
  not not_3 (not_3_out, LASTT);
  and and_5 (and_5_out, not_2_out, SUB_MOD2);
  and and_6 (and_6_out, not_3_out, CNT_EN2);
  or or_1 (or_1_out, decoder_1_out4, and_5_out);
  or or_2 (or_2_out, and_1_out, SHIFT2);
  or or_3 (or_3_out, or_1_out, or_5_out);
  or or_4 (or_4_out, CNT_CLR2, and_6_out);
  or or_5 (or_5_out, and_4_out, DONE);
  or or_6 (or_6_out, or_2_out, or_3_out);
  or or_7 (or_7_out, or_4_out, SHIFT2);
  or or_8 (or_8_out, SETQ0_OVER2, or_5_out);
  or or_9 (or_9_out, or_7_out, or_8_out);
  or or_10 (or_10_out, and_3_out, or_1_out);
  or or_11 (or_11_out, SETQ0_OVER2, or_5_out);
  or or_12 (or_12_out, or_10_out, or_11_out);
  or or_13 (RLOAD2, CNT_CLR2, decoder_1_out4);
  and and_7 (Q0_VAL2, SETQ0_OVER2, not_2_out);

  assign LOAD_DIV = CNT_CLR2;
  assign LOAD_Q = CNT_CLR2;
endmodule

module ctrl_fsm2 (
  input  START,
  input  CK,
  input  RESET,
  input  LAST,
  input  NEG,
  output CNT_CLR,
  output SHIFT,
  output SUB_MOD,
  output LOAD_DIV,
  output RLOAD,
  output LOAD_Q,
  output SETQ0_OVER,
  output Q0_VAL,
  output CNT_EN,
  output DONE
);

  wire and_1_out, and_2_out, and_3_out, decoder_1_out0, not_1_out, or_1_out, or_2_out, or_3_out, or_4_out,
       or_5_out, or_7_out;
  wire [2:0] dff_from_jk_1_q;

  // Probe on dff_from_jk_1_q[0]
  DFF_from_JK dff_from_jk_1 (.D(or_7_out), .CLK(CK), .RESET(RESET), .Q(dff_from_jk_1_q[0]));
  // Probe on dff_from_jk_1_q[1]
  DFF_from_JK dff_from_jk_2 (.D(or_4_out), .CLK(CK), .RESET(RESET), .Q(dff_from_jk_1_q[1]));
  DFF_from_JK dff_from_jk_3 (.D(or_5_out), .CLK(CK), .RESET(RESET), .Q(dff_from_jk_1_q[2]));
  // Probe on dff_from_jk_1_q[2]
  Decoder #(.select(3)) decoder_1 (
    .out0(decoder_1_out0), .out1(CNT_CLR), .out2(SHIFT), .out3(SUB_MOD), .out4(SETQ0_OVER), .out5(CNT_EN),
    .out6(DONE), .out7(DONE), .sel(dff_from_jk_1_q));  // open: en
  and and_1 (and_1_out, START, decoder_1_out0);
  or or_1 (or_1_out, CNT_CLR, SHIFT);
  and and_2 (and_2_out, CNT_EN, LAST);
  or or_2 (or_2_out, SUB_MOD, SETQ0_OVER);
  and and_3 (and_3_out, SETQ0_OVER, NEG);
  and and_4 (Q0_VAL, SETQ0_OVER, not_1_out);
  not not_1 (not_1_out, NEG);
  or or_3 (or_3_out, and_1_out, SHIFT);
  or or_4 (or_4_out, or_1_out, and_2_out);
  or or_5 (or_5_out, and_2_out, or_2_out);
  or or_6 (RLOAD, SUB_MOD, and_3_out);
  or or_7 (or_7_out, or_3_out, SETQ0_OVER);

  assign LOAD_DIV = CNT_CLR;
  assign LOAD_Q = CNT_CLR;
endmodule

module ctrl_fsm3 (
  input  START,
  input  CLK,
  input  RESET,
  input  LAST,
  input  NEG,
  output CNT_CLR,
  output LOAD_DIV,
  output LOAD_Q,
  output SHITF,
  output SUB,
  output DONE,
  output CNT_EN,
  output RLOAD,
  output Q0_VAL
);

  wire and_1_out, and_2_out, and_3_out, and_4_out, and_5_out, and_6_out, j_k_ff_1_q, j_k_ff_2_q, not_1_out,
       not_2_out, not_3_out, or_1_out, or_2_out;

  J_K_Flip_Flop j_k_ff_1 (.J(j_k_ff_2_q), .K(and_1_out), .clk(CLK), .Q(j_k_ff_1_q), .reset(RESET));  // open: Qn, preset
  J_K_Flip_Flop j_k_ff_2 (.J(or_2_out), .K(j_k_ff_2_q), .clk(CLK), .Q(j_k_ff_2_q), .reset(RESET));  // open: Qn, preset
  not not_1 (not_1_out, j_k_ff_1_q);
  not not_2 (not_2_out, j_k_ff_2_q);
  not not_3 (not_3_out, LAST);
  and and_1 (and_1_out, j_k_ff_2_q, LAST);
  and and_2 (and_2_out, START, not_1_out);
  and and_3 (and_3_out, j_k_ff_1_q, not_2_out);
  and and_4 (and_4_out, j_k_ff_1_q, j_k_ff_2_q);
  or or_1 (or_1_out, and_2_out, and_3_out);
  and and_5 (and_5_out, and_4_out, not_3_out);
  and and_6 (and_6_out, not_1_out, not_2_out);
  or or_2 (or_2_out, or_1_out, and_5_out);
  and and_7 (CNT_CLR, START, and_6_out);
  and and_8 (SUB, not_2_out, j_k_ff_1_q);
  and and_9 (CNT_EN, j_k_ff_2_q, j_k_ff_1_q);
  and and_10 (SHITF, not_1_out, j_k_ff_2_q);
  and and_11 (RLOAD, CNT_EN, NEG);
  not not_4 (Q0_VAL, NEG);
  and and_12 (DONE, LAST, CNT_EN);

  assign LOAD_DIV = CNT_CLR;
  assign LOAD_Q = CNT_CLR;
endmodule

module DATAPATH (
  input  CLK,
  input  Q0_VAL,
  input  RLOAD,
  input  DIVIDEND,
  input  SHIFT,
  input  [2:0] DIVISOR,
  output [7:0] REMAINDER,
  output NEG,
  output [7:0] QUOTIENT
);

  wire ctrl_fsm3_1_load_div, ctrl_fsm3_1_load_q, ctrl_fsm3_1_rload;
  wire [7:0] adder_1_out, bit_extender_1_out, M_q, multiplexer_1_out, multiplexer_2_out, subtractor_1_out;

  ctrl_fsm3 ctrl_fsm3_1 (
    .CLK(CLK), .LOAD_DIV(ctrl_fsm3_1_load_div), .LOAD_Q(ctrl_fsm3_1_load_q), .RLOAD(ctrl_fsm3_1_rload));  // open: START, RESET, LAST, NEG, CNT_CLR, SHITF, SUB, DONE, CNT_EN, Q0_VAL
  assign bit_extender_1_out = {{5{DIVISOR[2]}}, DIVISOR};  // Bit_Extender bit_extender_1
  Register A (.D(multiplexer_2_out), .en(1'b1), .clk(CLK), .Q(REMAINDER));  // open: clr
  Register Q (.D(multiplexer_1_out), .en(ctrl_fsm3_1_load_q), .clk(CLK), .Q(QUOTIENT));  // open: clr
  Register M (.D(bit_extender_1_out), .en(ctrl_fsm3_1_load_div), .clk(CLK), .Q(M_q));  // open: clr
  Multiplexer #(.width(8)) multiplexer_1 (
    .in0(QUOTIENT), .in1({QUOTIENT[6:0], Q0_VAL}), .out(multiplexer_1_out), .sel(SHIFT));
  Subtractor subtractor_1 (.a(REMAINDER), .b(M_q), .out(subtractor_1_out), .bout(NEG));  // open: bin
  Adder adder_1 (.a(subtractor_1_out), .b(M_q), .out(adder_1_out));  // open: cin, cout
  Multiplexer #(.width(8)) multiplexer_2 (
    .in0(subtractor_1_out), .in1(adder_1_out), .out(multiplexer_2_out), .sel(ctrl_fsm3_1_rload));
endmodule

module FIND_Q (
  input  [7:0] IN_1,
  input  [7:0] Q,
  input  LOAD,
  output [7:0] OUT_1
);

  Multiplexer multiplexer_1 (.in0(Q[0]), .in1(IN_1[0]), .out(OUT_1[0]), .sel(LOAD));
  Multiplexer multiplexer_2 (.in0(Q[1]), .in1(IN_1[1]), .out(OUT_1[1]), .sel(LOAD));
  Multiplexer multiplexer_3 (.in0(Q[2]), .in1(IN_1[2]), .out(OUT_1[2]), .sel(LOAD));
  Multiplexer multiplexer_4 (.in0(Q[3]), .in1(IN_1[3]), .out(OUT_1[3]), .sel(LOAD));
  Multiplexer multiplexer_5 (.in0(Q[4]), .in1(IN_1[4]), .out(OUT_1[4]), .sel(LOAD));
  Multiplexer multiplexer_6 (.in0(Q[5]), .in1(IN_1[5]), .out(OUT_1[5]), .sel(LOAD));
  Multiplexer multiplexer_7 (.in0(Q[6]), .in1(IN_1[6]), .out(OUT_1[6]), .sel(LOAD));
  Multiplexer multiplexer_8 (.in0(Q[7]), .in1(IN_1[7]), .out(OUT_1[7]), .sel(LOAD));
endmodule

module FIND_A (
  input  KEEP,
  input  [3:0] IN_1,
  input  [3:0] S,
  input  LOAD,
  input  [3:0] A,
  output [3:0] OUT_1
);

  wire multiplexer_1_out, multiplexer_2_out, multiplexer_3_out, multiplexer_4_out;

  Multiplexer multiplexer_1 (.in0(S[0]), .in1(IN_1[0]), .out(multiplexer_1_out), .sel(LOAD));
  Multiplexer multiplexer_2 (.in0(S[1]), .in1(IN_1[1]), .out(multiplexer_2_out), .sel(LOAD));
  Multiplexer multiplexer_3 (.in0(S[2]), .in1(IN_1[2]), .out(multiplexer_3_out), .sel(LOAD));
  Multiplexer multiplexer_4 (.in0(S[3]), .in1(IN_1[3]), .out(multiplexer_4_out), .sel(LOAD));
  Multiplexer multiplexer_5 (.in0(multiplexer_1_out), .in1(A[0]), .out(OUT_1[0]), .sel(KEEP));
  Multiplexer multiplexer_6 (.in0(multiplexer_2_out), .in1(A[1]), .out(OUT_1[1]), .sel(KEEP));
  Multiplexer multiplexer_7 (.in0(multiplexer_3_out), .in1(A[2]), .out(OUT_1[2]), .sel(KEEP));
  Multiplexer multiplexer_8 (.in0(multiplexer_4_out), .in1(A[3]), .out(OUT_1[3]), .sel(KEEP));
endmodule

module NEW_SHIFT (
  input  SERIAL,
  input  LOAD,
  input  I0,
  input  I1,
  input  I2,
  input  I3,
  input  I4,
  input  I5,
  input  I6,
  input  I7,
  input  I8,
  input  I9,
  input  I10,
  input  I11,
  output S0,
  output S1,
  output S2,
  output S3,
  output S4,
  output S5,
  output S6,
  output S7,
  output S8,
  output S9,
  output S10,
  output S11
);

  wire and_1_out, and_2_out, and_3_out, and_4_out, and_5_out, and_6_out, and_7_out, and_8_out, and_9_out,
       and_10_out, and_11_out, and_12_out, and_13_out, and_14_out, and_15_out, and_16_out, and_17_out,
       and_18_out, and_19_out, and_20_out, and_21_out, and_22_out, and_23_out, and_24_out, not_1_out,
       or_1_out, or_2_out, or_3_out, or_4_out, or_5_out, or_6_out, or_7_out, or_8_out, or_9_out, or_10_out,
       or_11_out, or_12_out;

  not not_1 (not_1_out, LOAD);
  and and_1 (and_1_out, SERIAL, LOAD);
  and and_2 (and_2_out, I0, not_1_out);
  and and_3 (and_3_out, S0, LOAD);
  and and_4 (and_4_out, I1, not_1_out);
  and and_5 (and_5_out, S1, LOAD);
  and and_6 (and_6_out, I2, not_1_out);
  and and_7 (and_7_out, S2, LOAD);
  and and_8 (and_8_out, I3, not_1_out);
  and and_9 (and_9_out, S3, LOAD);
  and and_10 (and_10_out, I4, not_1_out);
  and and_11 (and_11_out, S4, LOAD);
  and and_12 (and_12_out, I5, not_1_out);
  and and_13 (and_13_out, S5, LOAD);
  and and_14 (and_14_out, I6, not_1_out);
  and and_15 (and_15_out, S6, LOAD);
  and and_16 (and_16_out, I7, not_1_out);
  and and_17 (and_17_out, S7, LOAD);
  and and_18 (and_18_out, I8, not_1_out);
  and and_19 (and_19_out, S8, LOAD);
  and and_20 (and_20_out, I9, not_1_out);
  and and_21 (and_21_out, S9, LOAD);
  and and_22 (and_22_out, I10, not_1_out);
  and and_23 (and_23_out, S10, LOAD);
  and and_24 (and_24_out, I11, not_1_out);
  or or_1 (or_1_out, and_1_out, and_2_out);
  or or_2 (or_2_out, and_3_out, and_4_out);
  or or_3 (or_3_out, and_5_out, and_6_out);
  or or_4 (or_4_out, and_7_out, and_8_out);
  or or_5 (or_5_out, and_9_out, and_10_out);
  or or_6 (or_6_out, and_11_out, and_12_out);
  or or_7 (or_7_out, and_13_out, and_14_out);
  or or_8 (or_8_out, and_15_out, and_16_out);
  or or_9 (or_9_out, and_17_out, and_18_out);
  or or_10 (or_10_out, and_19_out, and_20_out);
  or or_11 (or_11_out, and_21_out, and_22_out);
  or or_12 (or_12_out, and_23_out, and_24_out);
  DFF_from_JK dff_from_jk_1 (.D(or_1_out), .Q(S0));  // open: CLK, RESET
  DFF_from_JK dff_from_jk_2 (.D(or_2_out), .Q(S1));  // open: CLK, RESET
  DFF_from_JK dff_from_jk_3 (.D(or_3_out), .Q(S2));  // open: CLK, RESET
  DFF_from_JK dff_from_jk_4 (.D(or_4_out), .Q(S3));  // open: CLK, RESET
  DFF_from_JK dff_from_jk_5 (.D(or_5_out), .Q(S4));  // open: CLK, RESET
  DFF_from_JK dff_from_jk_6 (.D(or_6_out), .Q(S5));  // open: CLK, RESET
  DFF_from_JK dff_from_jk_7 (.D(or_7_out), .Q(S6));  // open: CLK, RESET
  DFF_from_JK dff_from_jk_8 (.D(or_8_out), .Q(S7));  // open: CLK, RESET
  DFF_from_JK dff_from_jk_9 (.D(or_9_out), .Q(S8));  // open: CLK, RESET
  DFF_from_JK dff_from_jk_10 (.D(or_10_out), .Q(S9));  // open: CLK, RESET
  DFF_from_JK dff_from_jk_11 (.D(or_11_out), .Q(S10));  // open: CLK, RESET
  DFF_from_JK dff_from_jk_12 (.D(or_12_out), .Q(S11));  // open: CLK, RESET
endmodule
